// Digital circuit lab03_solution.dig as structural Verilog
module lab03_solution (
  input  clk,
  input  rst,
  output [31:0] PC,
  output [5:0] opcode,
  output [4:0] src1__addr,
  output [31:0] src1__out,
  output [4:0] src2__addr,
  output [31:0] src2__out,
  output [4:0] dst__addr,
  output [31:0] dst__data
);

  wire alu__src, and_1_out, branch, mem__read, mem__to__reg, mem__write, reg__dst, reg__write, zero;
  wire [1:0] alu__op;
  wire [3:0] u_alu_control_alu_control;
  wire [15:0] cpumemory_d2;
  wire [31:0] alu__result, data__val, multiplexer_3_out, multiplexer_4_out, next__PC, PC__offset,
       u_alu_2_result, u_alu_result;

  gen_register #(.applicationType("IVERILOG"), .CodeFile("/home/allan/cs161L/Lab03-SingleCycleDatapath/gen_register.v")) u_gen_register (
    .clk(clk), .rst(rst), .write_en(clk), .data_in(next__PC), .data_out(PC));
  alu #(.applicationType("IVERILOG"), .CodeFile("/home/allan/cs161L/Lab03-SingleCycleDatapath/alu.v")) u_alu (
    .alu_control(4'b0010), .A(PC), .B(32'h4), .result(u_alu_result));  // open: zero
  RAMDualAccess #(.AddrBits(8), .isProgramMemory("true"), .Bits(32)) cpumemory (
    .str(mem__write), .C(clk), .ld(mem__read), .A1(alu__result[7:0]), .Din1(src2__out), .A2(PC[9:2]),
    .D1(data__val), .D2({opcode, src1__addr, src2__addr, cpumemory_d2}));
  alu #(.applicationType("IVERILOG"), .CodeFile("/home/allan/cs161L/Lab03-SingleCycleDatapath/alu.v")) u_alu_2 (
    .alu_control(4'b0010), .A(u_alu_result), .B({PC__offset[31:2], 2'b00}), .result(u_alu_2_result));  // open: zero
  and and_1 (and_1_out, branch, zero);
  Multiplexer #(.Bits(32)) multiplexer_1 (.sel(and_1_out), .in_0(u_alu_result), .in_1(u_alu_2_result), .out(next__PC));
  BitExtender #(.inputBits(16), .outputBits(32)) bitextender_1 (.in(cpumemory_d2), .out(PC__offset));
  Multiplexer #(.Bits(5)) multiplexer_2 (
    .sel(reg__dst), .in_0(src2__addr), .in_1(cpumemory_d2[15:11]), .out(dst__addr));
  control_unit #(.applicationType("IVERILOG"), .CodeFile("/home/allan/cs161L/Lab03-SingleCycleDatapath/control_unit.v")) u_control_unit (
    .instr_op(opcode), .reg_dst(reg__dst), .branch(branch), .mem_read(mem__read), .mem_to_reg(mem__to__reg),
    .alu_op(alu__op), .mem_write(mem__write), .alu_src(alu__src), .reg_write(reg__write));
  cpu_registers #(.applicationType("IVERILOG"), .CodeFile("/home/allan/cs161L/Lab03-SingleCycleDatapath/cpu_registers.v")) u_cpu_registers (
    .clk(clk), .rst(rst), .write_en(reg__write), .src1_addr(src1__addr), .src2_addr(src2__addr),
    .dst_addr(dst__addr), .data_in(dst__data), .src1_out(src1__out), .src2_out(src2__out));
  alu_control #(.applicationType("IVERILOG"), .CodeFile("/home/allan/cs161L/Lab03-SingleCycleDatapath/alu_control.v")) u_alu_control (
    .alu_op(alu__op), .funct(cpumemory_d2[5:0]), .alu_control(u_alu_control_alu_control));
  Multiplexer #(.Bits(32)) multiplexer_3 (.sel(alu__src), .in_0(src2__out), .in_1(PC__offset), .out(multiplexer_3_out));
  alu #(.applicationType("IVERILOG"), .CodeFile("/home/allan/cs161L/Lab03-SingleCycleDatapath/alu.v")) u_alu_3 (
    .alu_control(u_alu_control_alu_control), .A(src1__out), .B(multiplexer_3_out), .zero(zero),
    .result(alu__result));
  Multiplexer #(.Bits(32)) multiplexer_4 (
    .sel(mem__to__reg), .in_0(alu__result), .in_1(data__val), .out(multiplexer_4_out));

  // Other names for the same wires on the sheet: mem__data[31:0] = src2__out; reg__data[31:0] = dst__data

  // Notes on the sheet:
  //   Inputs
  //   PC
  //   Outputs for testing
endmodule
