// Digital circuit lab04.dig as structural Verilog
module lab04 (
  input  clk,
  input  rst,
  output [31:0] PC,
  output [5:0] opcode,
  output [4:0] src1__addr,
  output [31:0] src1__out,
  output [4:0] src2__addr,
  output [31:0] src2__out,
  output [4:0] dst__addr,
  output [31:0] dst__data
);

  gen_register #(.applicationType("IVERILOG"), .CodeFile("/home/allan/cs161L/Lab03-SingleCycleDatapath/gen_register.v")) u_gen_register ();  // open: clk, rst, write_en, data_in, data_out
  alu #(.applicationType("IVERILOG"), .CodeFile("/home/allan/cs161L/Lab03-SingleCycleDatapath/alu.v")) u_alu ();  // open: alu_control, A, B, zero, result
  RAMDualAccess #(.AddrBits(8), .Bits(32), .isProgramMemory("true")) cpumemory ();  // open: str, C, ld, A1, Din1, A2, D1, D2
  alu #(.applicationType("IVERILOG"), .CodeFile("/home/allan/cs161L/Lab03-SingleCycleDatapath/alu.v")) u_alu_2 ();  // open: alu_control, A, B, zero, result
  // And and_1 is placed but not wired
  Multiplexer #(.Bits(32)) multiplexer_1 ();  // open: sel, in_0, in_1, out
  BitExtender #(.inputBits(16), .outputBits(32)) bitextender_1 ();  // open: in, out
  Multiplexer #(.Bits(5)) multiplexer_2 ();  // open: sel, in_0, in_1, out
  control_unit #(.applicationType("IVERILOG"), .CodeFile("/home/allan/cs161L/Lab03-SingleCycleDatapath/control_unit.v")) u_control_unit ();  // open: instr_op, reg_dst, branch, mem_read, mem_to_reg, alu_op, mem_write, alu_src, reg_write
  cpu_registers #(.applicationType("IVERILOG"), .CodeFile("/home/allan/cs161L/Lab03-SingleCycleDatapath/cpu_registers.v")) u_cpu_registers ();  // open: clk, rst, write_en, src1_addr, src2_addr, dst_addr, data_in, src1_out, src2_out
  alu_control #(.applicationType("IVERILOG"), .CodeFile("/home/allan/cs161L/Lab03-SingleCycleDatapath/alu_control.v")) u_alu_control ();  // open: alu_op, funct, alu_control
  Multiplexer #(.Bits(32)) multiplexer_3 ();  // open: sel, in_0, in_1, out
  alu #(.applicationType("IVERILOG"), .CodeFile("/home/allan/cs161L/Lab03-SingleCycleDatapath/alu.v")) u_alu_3 ();  // open: alu_control, A, B, zero, result
  Multiplexer #(.Bits(32)) multiplexer_4 ();  // open: sel, in_0, in_1, out

  // Notes on the sheet:
  //   Inputs
  //   PC
  //   Outputs for testing
endmodule
